# Fritzing sketch PROTOMODULO 1.1 (saved by Fritzing 0.9.3b)
circuit board: 5.10418cm x 5.96978cm
breadboards: 1

parts:
  AS3340 = IC, DIP package, 16 pins [chip_label=IC]
  TL072 = IC, DIP package, 8 pins [chip_label=IC]
  100K = Resistor [tolerance=±5% resistance=100k package=THT]
  100K_2 = Resistor [tolerance=±5% resistance=100k package=THT]
  470R = Resistor [tolerance=±5% resistance=470 package=THT]
  10n = Ceramic Capacitor [capacitance=10nF package="100 mil [THT, multilayer]"]
  1K8 = Resistor [tolerance=±5% resistance=1.8k package=THT]
  1n = Ceramic Capacitor [capacitance=100nF package="100 mil [THT, multilayer]"]
  470R_2 = Resistor [tolerance=±5% resistance=470 package=THT]
  1M5 = Resistor [tolerance=±5% resistance=1.5M package=THT]
  22K = Resistor [tolerance=±5% resistance=22k package=THT]
  5_6K = Resistor [tolerance=±5% resistance=5.6k package=THT]
  620R = Resistor [tolerance=±5% resistance=620 package=THT]
  R12 = TRIMPOT [package=3362u-2]
  R13 = Rotary Potentiometer (Large) [maximum_resistance=100kΩ package=THT]
  J4 = 3.5mm Switch Jack [part_number=PJ301M-12]
  J5 = 3.5mm Switch Jack [part_number=PJ301M-12]
  J6 = 3.5mm Switch Jack [part_number=PJ301M-12]
  J1 = female pin header, 5 pins [form="♀ (female)"]

nets:
  N1: AS3340.pin1, 22K.Pin_0
  N2: AS3340.pin2, 5_6K.Pin_1
  N3: AS3340.pin3, 5_6K.Pin_0, 620R.Pin_1, R12.WIPER, R12.CW
  N4: AS3340.pin8, TL072.pin3
  N5: AS3340.pin10, TL072.pin5
  N6: AS3340.pin11, 1n.0
  GND: AS3340.pin12, 10n.1, 1K8.Pin_1, 1n.1, 470R_2.Pin_0, J4.Pin_1, J5.Pin_1, J6.Pin_1, J1.pin2, J1.pin3, J1.pin4
  N7: AS3340.pin13, 470R_2.Pin_1, 1M5.Pin_0
  N8: AS3340.pin14, 1K8.Pin_0
  N9: AS3340.pin15, 100K.Pin_1, 100K_2.Pin_1, 470R.Pin_1
  12V: AS3340.pin16, TL072.pin8, 1M5.Pin_1, R13.leg2, J1.pin1
  N10: TL072.pin1, TL072.pin2, J4.Pin_3
  N11: TL072.pin4, 620R.Pin_0, J1.pin5
  N12: TL072.pin6, TL072.pin7, J5.Pin_3
  N13: 100K.Pin_0, J6.Pin_3
  N14: 100K_2.Pin_0, R13.wiper
  N15: 470R.Pin_0, 10n.0
  N16: 22K.Pin_1, R12.CCW

notes:
  audio_cmm_cenart
  2019
  3340VCO

custom parts:
  3.5mm Switch Jack: Thonkiconn 3.5mm switching Jack
